# Fritzing sketch OilTankGaurd (saved by Fritzing 1.0.5)
breadboards: 1

parts:
  U1 = XIAO ESP32C6 [part_number=" XIAO ESP32C6"]
  M1 = 1 chan 5v relay module
  Bat2 = battery_holder_single_18650
  Part1 = Adafruit MiniBoost 5V 100mA Charge Pump AP3602A [part_number=3661]
  A1 = xkc-25y-v [package=THT]
  Part2 = Solar Panel [package="Renogy 50 Watts 12 Volt Monocrystalline Bendable Solar Panel"]
  A2 = CN3065 Mini Solar Charger Module

nets:
  N1: U1.D0, A1.pin3
  N2: U1.D6, M1.pin_3
  N3: U1.GND, M1.pin_2, Part1.!SHDN, A1.pin2
  N4: U1.5V, M1.pin_1, M1.pin_4, Part1.5.0V
  N5: M1.pin_5, A1.pin4
  N6: Bat2.+#0, Part1.VIN, Part2.Connector_2, A2.Pin_2, A2.Pin_10, A2.Pin_12
  N7: Bat2.+#1, A2.Pin_11
  N8: Part1.GND, A2.Pin_9

custom parts:
  XIAO ESP32C6: XIAO ESP32C6 is a cost-effective MCU based on Espressif’s ESP32-C6. This compact MCU excels in Matter-compliant smart home applications with its support for various wireless connectivity (2.4GHz Wi-Fi 6, BLE 5.0, Zigbee, and Thread). Designed with the thumb-size footprint and a single-sided mount of the XIAO Series, it's perfect for space-limited projects. Encrypted on the chip, the XIAO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
  1 chan 5v relay module: 1 Channel 5V Relay Module Board Shield with Optocoupler Support High and Low Level Trigger for Arduino.
  battery_holder_single_18650: single 18650 battery holder
  Adafruit MiniBoost 5V 100mA Charge Pump AP3602A: This adorable little board will come in very handy whenever you need a small amount of 5V power. It's the size of a linear regulator, but it's actually a mini-booster! Input 3V on one side, and get 5V at up to 100mA supply on the other. Perfect for use with battery-powered projects with 2 or 3 Alkaline, or a single Lithium battery. This booster uses a charge-pump topology, which makes it very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
  xkc-25y-v: XKC-Y25-v Non-Contact Liquid Level Sensor IP67 Waterproof Water Level Detector DC 5-12V. Note this version has the plug reversed to match the connector on the DFrobot sens0204 interface board, thus the connector labels on the device are opposite of the connectors on the output connector.
  Solar Panel: Renogy 50 Watts 12 Volt Solar Panel
  CN3065 Mini Solar Charger Module: CN3791 MPPT Solar Panel Regulator Controller 6V 9V 12V 1 Zelle Lithium-Batterie Ladung Solar Panel Ladegerät board-Controller Module.
